# Fritzing sketch Scuola (saved by Fritzing 0.9.3b)
breadboards: 1

parts:
  Componente1 = Arduino Uno (Rev3)
  U1 = TEMPERATURE-SENSOR [package=to-92]
  LCD1 = LCD screen
  VCC1 = Battery

nets:
  N1: Componente1.A0, U1.GND
  N2: Componente1.D10_PWM/SS, LCD1.DB0
  N3: Componente1.D11_PWM/MOSI, LCD1.E
  N4: Componente1.D12/MISO, LCD1.R/W
  N5: Componente1.D13/SCK, LCD1.RS
  N6: Componente1.GND, LCD1.V0, VCC1.-, VCC1.+
  N7: Componente1.AREF, LCD1.VDD
  N8: Componente1.A4/SDA, LCD1.VSS
